# Fritzing sketch Neon Timer (saved by Fritzing 0.9.3b)
circuit board: 8.46667cm x 5.64444cm
breadboards: 1

parts:
  LCD1 = LCD screen
  元件1 = Arduino Pro Mini v13
  VCC1 = Battery
  S1 = SPST Switch [package=switch-spdt_kit]
  S2 = Pushbutton [package="[SMD]"]
  R1 = Resistor [tolerance=±5% resistance=10k package="2512 [SMD]"]
  U2 = TOUCH [package=touch2]
  U3 = TOUCH [package=touch2]

nets:
  VSS: LCD1.VSS, LCD1.V0, LCD1.R/W, LCD1.LED-, 元件1.GND, VCC1.-, S1.O, R1.Pin_0
  VDD: LCD1.VDD, 元件1.VCC, VCC1.+, S2.Pin_3, S2.Pin_4, U2.T2, U3.T2
  N1: LCD1.RS, 元件1.D12/MISO
  N2: LCD1.E, 元件1.D11_PWM/MOSI
  N3: LCD1.DB4, 元件1.D5_PWM
  N4: LCD1.DB5, 元件1.D4
  N5: LCD1.DB6, 元件1.D3_PWM
  N6: LCD1.DB7, 元件1.D2
  N7: LCD1.LED+, S1.S
  N8: 元件1.D8, S2.Pin_1, S2.Pin_2, R1.Pin_1
  N9: 元件1.D7, U3.T1
  N10: 元件1.D6_PWM, U2.T1
